# Fritzing sketch ScareOS (saved by Fritzing 0.9.2b)
breadboards: 1

parts:
  Bauteil1 = Arduino Pro Mini v13
  R1 = Resistor [tolerance=±5% resistance=563 package=THT]
  Bauteil2 = SRF05 Ultrasonic Rangefinder
  R2 = Resistor [tolerance=±5% resistance=360 package=THT]
  LED1 = 8x8 LED Matrix (yellow)
  LED2 = 8x8 LED Matrix (yellow)
  Bauteil3 = Audio FX Sound Board
  SP1 = SPEAKER [package=pcb_mount_speaker]
  C1 = Electrolytic Capacitor [capacitance=470µF voltage=20V package="100 mil [THT, electrolytic]"]

nets (from the breadboard view):
  VCC: Bauteil1.VCC, Bauteil2.VCC, LED1.+, LED1.-, LED2.+, Bauteil3.VIN, C1.+
  N1: Bauteil1.A4, LED1.D, LED2.D
  N2: Bauteil1.A5, LED1.C, LED2.C
  GND: Bauteil1.GND, R1.Pin_0, Bauteil2.GND, LED2.-, Bauteil3.GND, Bauteil3.VBUS, SP1.-, C1.-
  N3: Bauteil1.D9_PWM, Bauteil3.1
  N4: Bauteil1.D8, Bauteil3.2
  N5: Bauteil1.D7, Bauteil3.3
  N6: Bauteil1.D6_PWM, Bauteil3.4
  N7: Bauteil1.D5_PWM, Bauteil3.ACT
  N8: Bauteil1.D3_PWM, Bauteil2.Trig
  N9: Bauteil1.D2, R1.Pin_1, R2.Pin_0
  N10: Bauteil2.Echo, R2.Pin_1
  N11: Bauteil3.L, SP1.+

custom parts:
  8x8 LED Matrix (yellow): 8x8 LED Matrix with I2C control (yellow)
  Audio FX Sound Board: The Adafruit Sound Board, the fastest way to add audio effects to a project!
